// Logisim project mips.circ as structural Verilog: 7 circuits, main circuit ALU
module RegisterFile (
  input  Write_ENABLE,
  input  [3:0] WriteReg,
  input  [3:0] ReadReg1,
  input  [3:0] ReadReg2,
  input  [25:0] in_5,
  input  Clock,
  output [25:0] out_7,
  output [25:0] out_8
);

  wire and_1_out, and_2_out, and_3_out, and_4_out, and_5_out, and_6_out, and_7_out, and_8_out, and_9_out,
       and_10_out, and_11_out, and_12_out, and_13_out, and_14_out, and_15_out, and_16_out, decoder_1_out0,
       decoder_1_out1, decoder_1_out2, decoder_1_out3, decoder_1_out4, decoder_1_out5, decoder_1_out6,
       decoder_1_out7, decoder_1_out8, decoder_1_out9, decoder_1_out10, decoder_1_out11, decoder_1_out12,
       decoder_1_out13, decoder_1_out14, decoder_1_out15;
  wire [25:0] register_1_q, register_2_q, register_3_q, register_4_q, register_5_q, register_6_q,
       register_7_q, register_8_q, register_9_q, register_10_q, register_11_q, register_12_q, register_13_q,
       register_14_q, register_15_q, register_16_q;

  Decoder #(.select(4), .disabled(0), .enable("false")) decoder_1 (
    .out0(decoder_1_out0), .out1(decoder_1_out1), .out2(decoder_1_out2), .out3(decoder_1_out3),
    .out4(decoder_1_out4), .out5(decoder_1_out5), .out6(decoder_1_out6), .out7(decoder_1_out7),
    .out8(decoder_1_out8), .out9(decoder_1_out9), .out10(decoder_1_out10), .out11(decoder_1_out11),
    .out12(decoder_1_out12), .out13(decoder_1_out13), .out14(decoder_1_out14), .out15(decoder_1_out15),
    .sel(WriteReg));
  and and_1 (and_1_out, Write_ENABLE, decoder_1_out0);
  and and_2 (and_2_out, Write_ENABLE, decoder_1_out1);
  and and_3 (and_3_out, Write_ENABLE, decoder_1_out2);
  and and_4 (and_4_out, Write_ENABLE, decoder_1_out3);
  and and_5 (and_5_out, Write_ENABLE, decoder_1_out4);
  and and_6 (and_6_out, Write_ENABLE, decoder_1_out5);
  and and_7 (and_7_out, Write_ENABLE, decoder_1_out6);
  and and_8 (and_8_out, Write_ENABLE, decoder_1_out7);
  and and_9 (and_9_out, Write_ENABLE, decoder_1_out8);
  and and_10 (and_10_out, Write_ENABLE, decoder_1_out9);
  and and_11 (and_11_out, Write_ENABLE, decoder_1_out10);
  and and_12 (and_12_out, Write_ENABLE, decoder_1_out11);
  and and_13 (and_13_out, Write_ENABLE, decoder_1_out12);
  and and_14 (and_14_out, Write_ENABLE, decoder_1_out13);
  and and_15 (and_15_out, Write_ENABLE, decoder_1_out14);
  and and_16 (and_16_out, Write_ENABLE, decoder_1_out15);
  Register #(.width(26)) register_1 (.D(in_5), .en(and_1_out), .Q(register_1_q), .clk(Clock));  // open: clr
  Register #(.width(26)) register_2 (.D(in_5), .en(and_2_out), .Q(register_2_q), .clk(Clock));  // open: clr
  Register #(.width(26)) register_3 (.D(in_5), .en(and_3_out), .Q(register_3_q), .clk(Clock));  // open: clr
  Register #(.width(26)) register_4 (.D(in_5), .en(and_4_out), .Q(register_4_q), .clk(Clock));  // open: clr
  Register #(.width(26)) register_5 (.D(in_5), .en(and_5_out), .Q(register_5_q), .clk(Clock));  // open: clr
  Register #(.width(26)) register_6 (.D(in_5), .en(and_6_out), .Q(register_6_q), .clk(Clock));  // open: clr
  Register #(.width(26)) register_7 (.D(in_5), .en(and_7_out), .Q(register_7_q), .clk(Clock));  // open: clr
  Register #(.width(26)) register_8 (.D(in_5), .en(and_8_out), .Q(register_8_q), .clk(Clock));  // open: clr
  Register #(.width(26)) register_9 (.D(in_5), .en(and_9_out), .Q(register_9_q), .clk(Clock));  // open: clr
  Register #(.width(26)) register_10 (.D(in_5), .en(and_10_out), .Q(register_10_q), .clk(Clock));  // open: clr
  Register #(.width(26)) register_11 (.D(in_5), .en(and_11_out), .Q(register_11_q), .clk(Clock));  // open: clr
  Register #(.width(26)) register_12 (.D(in_5), .en(and_12_out), .Q(register_12_q), .clk(Clock));  // open: clr
  Register #(.width(26)) register_13 (.D(in_5), .en(and_13_out), .Q(register_13_q), .clk(Clock));  // open: clr
  Register #(.width(26)) register_14 (.D(in_5), .en(and_14_out), .Q(register_14_q), .clk(Clock));  // open: clr
  Register #(.width(26)) register_15 (.D(in_5), .en(and_15_out), .Q(register_15_q), .clk(Clock));  // open: clr
  Register #(.width(26)) register_16 (.D(in_5), .en(and_16_out), .Q(register_16_q), .clk(Clock));  // open: clr
  Multiplexer #(.select(4), .width(26), .disabled(0), .enable("false")) multiplexer_1 (
    .in0(register_1_q), .in1(register_2_q), .in2(register_3_q), .in3(register_4_q), .in4(register_5_q),
    .in5(register_6_q), .in6(register_7_q), .in7(register_8_q), .in8(register_9_q), .in9(register_10_q),
    .in10(register_11_q), .in11(register_12_q), .in12(register_13_q), .in13(register_14_q),
    .in14(register_15_q), .in15(register_16_q), .out(out_7), .sel(ReadReg1));
  Multiplexer #(.select(4), .width(26), .disabled(0), .enable("false")) multiplexer_2 (
    .in0(register_1_q), .in1(register_2_q), .in2(register_3_q), .in3(register_4_q), .in4(register_5_q),
    .in5(register_6_q), .in6(register_7_q), .in7(register_8_q), .in8(register_9_q), .in9(register_10_q),
    .in10(register_11_q), .in11(register_12_q), .in12(register_13_q), .in13(register_14_q),
    .in14(register_15_q), .in15(register_16_q), .out(out_8), .sel(ReadReg2));

  // Notes on the sheet:
  //   WriteData
  //   RegisterData1
  //   RegisterData2
endmodule

module ALU (
  input  [25:0] in_1,
  input  [25:0] in_2,
  input  [4:0] ALU_OP,
  output [25:0] out_4,
  output out_5
);

  wire comparator_1_lt, comparator_2_eq, comparator_2_gt, comparator_2_lt;
  wire [4:0] bit_extender_2_out, bit_extender_3_out;
  wire [25:0] adder_1_out, and_1_out, bit_extender_1_out, bit_extender_4_out, bit_extender_5_out,
       bit_extender_6_out, divider_1_out, divider_1_rem, multiplier_1_cout, multiplier_1_out, nand_1_out,
       nor_1_out, nor_2_out, not_1_out, not_2_out, or_1_out, or_2_out, or_3_out, shifter_1_out,
       shifter_2_out, subtractor_1_out, xnor_1_out, xor_1_out;

  assign and_1_out = in_1 & in_2;  // AND_Gate and_1, 26 bits wide
  assign or_1_out = in_1 | in_2;  // OR_Gate or_1, 26 bits wide
  Adder #(.width(26)) adder_1 (.a(in_1), .b(in_2), .out(adder_1_out));  // open: cin, cout
  Subtractor #(.width(26)) subtractor_1 (.a(in_1), .b(in_2), .out(subtractor_1_out));  // open: bin, bout
  Comparator #(.width(26)) comparator_1 (.a(in_1), .b(in_2), .lt(comparator_1_lt));  // open: gt, eq
  assign bit_extender_1_out = {{25{1'b0}}, comparator_1_lt};  // Bit_Extender bit_extender_1
  assign xor_1_out = in_1 ^ in_2;  // XOR_Gate xor_1, 26 bits wide
  assign xnor_1_out = ~(in_1 ^ in_2);  // XNOR_Gate xnor_1, 26 bits wide
  assign nor_1_out = ~(in_1 | in_2);  // NOR_Gate nor_1, 26 bits wide
  assign nand_1_out = ~(in_1 & in_2);  // NAND_Gate nand_1, 26 bits wide
  assign not_1_out = ~in_1;  // NOT_Gate not_1, 26 bits wide
  assign not_2_out = ~in_2;  // NOT_Gate not_2, 26 bits wide
  Comparator #(.width(26)) comparator_2 (
    .a(in_1), .b(in_2), .gt(comparator_2_gt), .eq(comparator_2_eq), .lt(comparator_2_lt));
  Bit_Extender #(.in_width(26), .out_width(5)) bit_extender_2 (.in(in_2), .out(bit_extender_2_out));
  Bit_Extender #(.in_width(26), .out_width(5)) bit_extender_3 (.in(in_2), .out(bit_extender_3_out));
  Multiplier #(.width(26)) multiplier_1 (
    .a(in_1), .b(in_2), .out(multiplier_1_out), .cout(multiplier_1_cout));  // open: cin
  Divider #(.width(26)) divider_1 (.a(in_1), .b(in_2), .out(divider_1_out), .rem(divider_1_rem));  // open: upper
  assign bit_extender_4_out = {{25{1'b0}}, comparator_2_gt};  // Bit_Extender bit_extender_4
  assign bit_extender_5_out = {{25{1'b0}}, comparator_2_eq};  // Bit_Extender bit_extender_5
  assign or_2_out = bit_extender_5_out | bit_extender_6_out;  // OR_Gate or_2, 26 bits wide
  assign bit_extender_6_out = {{25{1'b0}}, comparator_2_lt};  // Bit_Extender bit_extender_6
  Shifter #(.width(26)) shifter_1 (.in(in_1), .\dist (bit_extender_2_out), .out(shifter_1_out));
  Shifter #(.width(26), .shift("lr")) shifter_2 (.in(in_1), .\dist (bit_extender_3_out), .out(shifter_2_out));
  assign or_3_out = bit_extender_4_out | bit_extender_5_out;  // OR_Gate or_3, 26 bits wide
  Multiplexer #(.select(5), .width(26), .disabled(0), .enable("false")) multiplexer_1 (
    .in0(and_1_out), .in1(or_1_out), .in2(adder_1_out), .in3(subtractor_1_out), .in4(bit_extender_1_out),
    .in5(xor_1_out), .in6(xnor_1_out), .in7(nor_1_out), .in8(nand_1_out), .in9(in_1), .in10(in_2),
    .in11(not_1_out), .in12(not_2_out), .in13(bit_extender_4_out), .in14(or_2_out), .in15(or_3_out),
    .in16(shifter_1_out), .in17(shifter_2_out), .in18(multiplier_1_out), .in19(multiplier_1_cout),
    .in20(divider_1_out), .in21(divider_1_rem), .in22({26{1'b0}}), .in23({26{1'b0}}), .in24({26{1'b0}}),
    .in25({26{1'b0}}), .in26({26{1'b0}}), .in27({26{1'b0}}), .in28({26{1'b0}}), .in29({26{1'b0}}),
    .in30({26{1'b0}}), .in31({26{1'b0}}), .out(out_4), .sel(ALU_OP));
  assign nor_2_out = ~(out_4 | out_4 | out_4 | out_4 | out_4 | out_4 | out_4 | out_4 | out_4 | out_4 | out_4 | out_4 | out_4 | out_4 | out_4 | out_4 | out_4 | out_4 | out_4 | out_4 | out_4 | out_4 | out_4 | out_4 | out_4 | out_4);  // NOR_Gate nor_2, 26 bits wide
  Bit_Extender #(.in_width(26), .out_width(1)) bit_extender_7 (.in(nor_2_out), .out(out_5));

  // Notes on the sheet:
  //   A
  //   B
  //   AND
  //   OR
  //   ADD
  //   SUB
  //   XOR
  //   XNOR
  //   NOR
  //   NAND
  //   PASS A
  //   PASS B
  //   NOT A
  //   NOT B
  //   SHİFT LEFT LOGİCAL
  //   SHİFT RİGHT LOGİCAL
  //   OUT
  //   ZERO
endmodule

module ROM (
  input  [25:0] in_1,
  output [25:0] out_2
);

  wire decoder_1_out0, decoder_1_out1, decoder_1_out2, decoder_1_out3;
  wire [25:0] rom_1_data, rom_2_data, rom_3_data, rom_4_data;

  Decoder #(.select(2), .disabled(0)) decoder_1 (
    .out0(decoder_1_out0), .out1(decoder_1_out1), .out2(decoder_1_out2), .out3(decoder_1_out3),
    .sel(in_1[25:24]));  // open: en
  ROM_part #(.addrWidth(24), .dataWidth(26)) rom_1 (.addr(in_1[23:0]), .data(rom_1_data), .sel(decoder_1_out0));
  ROM_part #(.addrWidth(24), .dataWidth(26)) rom_2 (.addr(in_1[23:0]), .data(rom_2_data), .sel(decoder_1_out1));
  ROM_part #(.addrWidth(24), .dataWidth(26)) rom_3 (.addr(in_1[23:0]), .data(rom_3_data), .sel(decoder_1_out2));
  ROM_part #(.addrWidth(24), .dataWidth(26)) rom_4 (.addr(in_1[23:0]), .data(rom_4_data), .sel(decoder_1_out3));
  Multiplexer #(.select(2), .width(26), .disabled(0)) multiplexer_1 (
    .in0(rom_1_data), .in1(rom_2_data), .in2(rom_3_data), .in3(rom_4_data), .out(out_2), .sel(in_1[25:24]));  // open: en

  // Notes on the sheet:
  //   ADRESS
endmodule

module RAM (
  input  [25:0] in_1,
  input  [25:0] in_2,
  input  MemWrite,
  input  MemRead,
  input  in_5,
  output [25:0] out_6
);

  wire decoder_1_out0, decoder_1_out1, decoder_1_out2, decoder_1_out3, not_1_out, not_2_out, not_3_out,
       not_4_out;
  wire [25:0] ram_1_data, ram_2_data, ram_3_data, ram_4_data;

  Decoder #(.select(2), .disabled(0)) decoder_1 (
    .out0(decoder_1_out0), .out1(decoder_1_out1), .out2(decoder_1_out2), .out3(decoder_1_out3),
    .sel(in_1[25:24]));  // open: en
  not not_1 (not_1_out, in_5);
  not not_2 (not_2_out, in_5);
  not not_3 (not_3_out, in_5);
  not not_4 (not_4_out, in_5);
  RAM_part #(.addrWidth(24), .dataWidth(26), .bus("separate")) ram_1 (
    .addr(in_1[23:0]), .din(in_2), .data(ram_1_data), .str(MemWrite), .sel(decoder_1_out0), .clk(not_1_out),
    .ld(MemRead));  // open: clr
  RAM_part #(.addrWidth(24), .dataWidth(26), .bus("separate")) ram_2 (
    .addr(in_1[23:0]), .din(in_2), .data(ram_2_data), .str(MemWrite), .sel(decoder_1_out1), .clk(not_4_out),
    .ld(MemRead));  // open: clr
  RAM_part #(.addrWidth(24), .dataWidth(26), .bus("separate")) ram_3 (
    .addr(in_1[23:0]), .din(in_2), .data(ram_3_data), .str(MemWrite), .sel(decoder_1_out2), .clk(not_2_out),
    .ld(MemRead));  // open: clr
  RAM_part #(.addrWidth(24), .dataWidth(26), .bus("separate")) ram_4 (
    .addr(in_1[23:0]), .din(in_2), .data(ram_4_data), .str(MemWrite), .sel(decoder_1_out3), .clk(not_3_out),
    .ld(MemRead));  // open: clr
  Multiplexer #(.select(2), .width(26), .disabled(0)) multiplexer_1 (
    .in0(ram_1_data), .in1(ram_2_data), .in2(ram_3_data), .in3(ram_4_data), .out(out_6), .sel(in_1[25:24]));  // open: en

  // Notes on the sheet:
  //   MemWrite: pull=down
  //   MemRead: pull=down
  //   ADDRESS
  //   DATA
endmodule

module ControlUnit (
  input  Op3,
  input  Op2,
  input  Op1,
  input  Op0,
  output RegDst,
  output ALUSrc,
  output Jump,
  output MemtoReg,
  output RegWrite,
  output MemRead,
  output MemWrite,
  output Branch,
  output ALUOp1,
  output ALUOp0,
  output jr,
  output jal
);

  wire and_1_out, and_2_out, and_3_out, and_4_out, and_5_out, and_6_out, and_7_out, and_8_out, and_9_out,
       and_10_out, and_11_out, and_12_out, and_13_out, and_14_out, and_15_out, and_16_out, and_17_out,
       and_18_out, and_19_out, and_20_out, and_21_out, and_22_out, and_23_out, and_24_out, and_25_out,
       and_27_out, and_28_out, and_31_out, and_32_out, and_33_out, and_34_out, and_42_out, not_1_out,
       not_2_out, not_3_out, not_4_out, not_5_out, not_6_out, not_7_out, not_8_out, not_9_out, not_10_out,
       not_11_out, not_12_out, not_13_out, not_14_out, not_15_out, not_16_out, not_17_out, not_18_out,
       not_19_out, not_20_out, not_21_out, not_22_out, not_23_out, not_24_out, not_25_out, not_26_out,
       not_27_out, not_28_out, not_29_out, not_30_out, not_31_out, not_32_out, not_33_out, not_34_out,
       not_35_out, or_2_out;

  not not_1 (not_1_out, Op3);
  and and_1 (and_1_out, not_1_out, not_2_out);
  not not_2 (not_2_out, Op2);
  not not_3 (not_3_out, Op1);
  and and_2 (and_2_out, not_3_out, not_4_out);
  not not_4 (not_4_out, Op0);
  not not_5 (not_5_out, Op2);
  and and_3 (and_3_out, not_5_out, Op1);
  and and_4 (and_4_out, Op3, not_6_out);
  not not_6 (not_6_out, Op2);
  not not_7 (not_7_out, Op1);
  and and_5 (and_5_out, not_7_out, not_8_out);
  not not_8 (not_8_out, Op0);
  not not_9 (not_9_out, Op3);
  and and_6 (and_6_out, not_9_out, Op1);
  not not_10 (not_10_out, Op0);
  not not_11 (not_11_out, Op3);
  and and_7 (and_7_out, not_11_out, not_12_out);
  not not_12 (not_12_out, Op2);
  and and_8 (and_8_out, Op1, Op0);
  not not_13 (not_13_out, Op2);
  and and_9 (and_9_out, not_13_out, not_14_out);
  not not_14 (not_14_out, Op1);
  not not_15 (not_15_out, Op0);
  not not_16 (not_16_out, Op3);
  and and_10 (and_10_out, not_16_out, not_17_out);
  not not_17 (not_17_out, Op2);
  and and_11 (and_11_out, Op1, Op0);
  not not_18 (not_18_out, Op3);
  not not_19 (not_19_out, Op0);
  not not_20 (not_20_out, Op3);
  and and_12 (and_12_out, not_20_out, not_21_out);
  not not_21 (not_21_out, Op2);
  and and_13 (and_13_out, Op1, Op0);
  and and_14 (and_14_out, Op3, not_22_out);
  not not_22 (not_22_out, Op2);
  and and_15 (and_15_out, Op1, Op0);
  not not_23 (not_23_out, Op3);
  and and_16 (and_16_out, not_23_out, Op2);
  not not_24 (not_24_out, Op1);
  and and_17 (and_17_out, not_24_out, not_25_out);
  not not_25 (not_25_out, Op0);
  not not_26 (not_26_out, Op3);
  and and_18 (and_18_out, not_26_out, not_27_out);
  not not_27 (not_27_out, Op2);
  not not_28 (not_28_out, Op1);
  and and_19 (and_19_out, not_28_out, not_29_out);
  not not_29 (not_29_out, Op0);
  not not_30 (not_30_out, Op3);
  and and_20 (and_20_out, not_30_out, Op2);
  not not_31 (not_31_out, Op1);
  and and_21 (and_21_out, not_31_out, not_32_out);
  not not_32 (not_32_out, Op0);
  not not_33 (not_33_out, Op3);
  and and_22 (and_22_out, not_33_out, Op2);
  and and_23 (and_23_out, Op1, Op0);
  not not_34 (not_34_out, Op3);
  and and_24 (and_24_out, not_34_out, Op2);
  and and_25 (and_25_out, Op1, not_35_out);
  not not_35 (not_35_out, Op0);
  and and_26 (RegDst, and_1_out, and_2_out);
  and and_27 (and_27_out, and_3_out, Op0);
  and and_28 (and_28_out, and_4_out, and_5_out);
  and and_29 (Jump, and_6_out, not_10_out);
  and and_30 (MemtoReg, and_7_out, and_8_out);
  and and_31 (and_31_out, and_9_out, not_15_out);
  and and_32 (and_32_out, and_10_out, and_11_out);
  and and_33 (and_33_out, not_18_out, Op2);
  and and_34 (and_34_out, Op1, not_19_out);
  and and_35 (MemRead, and_12_out, and_13_out);
  and and_36 (MemWrite, and_14_out, and_15_out);
  and and_37 (Branch, and_16_out, and_17_out);
  and and_38 (ALUOp1, and_18_out, and_19_out);
  and and_39 (ALUOp0, and_20_out, and_21_out);
  and and_40 (jr, and_22_out, and_23_out);
  and and_41 (jal, and_24_out, and_25_out);
  or or_1 (ALUSrc, and_27_out, and_28_out);
  or or_2 (or_2_out, and_31_out, and_32_out);
  and and_42 (and_42_out, and_33_out, and_34_out);
  or or_3 (RegWrite, or_2_out, and_42_out);
endmodule

module ALUControl (
  input  [4:0] Function,
  input  [1:0] ALUOp,
  output [4:0] ALUControl
);

  wire [4:0] rom_1_data;

  ROM_part #(.addrWidth(5), .dataWidth(5)) rom_1 (.addr(Function), .data(rom_1_data));  // open: sel
  Multiplexer #(.select(2), .width(5), .disabled(0)) multiplexer_1 (
    .in0(5'b00010), .in1(5'b00011), .in2(rom_1_data), .in3({5{1'b0}}), .out(ALUControl), .sel(ALUOp));  // open: en

  // Notes on the sheet:
  //   Function: pull=down
  //   ROM
  //   contents of rom_1 (hex, n*v repeats v):
  //   0 1 2 3 4 5 6 7 8 9 a b c d e f 10 11 12 13 14 15 9*16 6
endmodule

module Pc (
);

  wire alu_1_out_5, and_1_out, clock_1_out, controlunit_1_alusrc, controlunit_1_branch, controlunit_1_jal,
       controlunit_1_jr, controlunit_1_jump, controlunit_1_memread, controlunit_1_memtoreg,
       controlunit_1_memwrite, controlunit_1_regdst, controlunit_1_regwrite;
  wire [1:0] controlunit_1_aluop0;
  wire [3:0] multiplexer_3_out;
  wire [4:0] alucontrol_1_alucontrol;
  wire [11:0] adder_1_out;
  wire [13:0] adder_1_out_2, rom_1_out_2;
  wire [25:0] adder_2_out, alu_1_out_4, bit_extender_1_out, multiplexer_1_out, multiplexer_2_out,
       multiplexer_4_out, multiplexer_5_out, multiplexer_6_out, multiplexer_7_out, multiplexer_8_out,
       ram_1_out_6, register_1_q, registerfile_1_out_7, registerfile_1_out_8;
  wire [25:14] rom_1_out_2_2;

  Register #(.width(26)) register_1 (.D(multiplexer_7_out), .Q(register_1_q), .clk(clock_1_out));  // open: en, clr
  Clock clock_1 (.out(clock_1_out));
  Adder #(.width(26)) adder_1 (
    .a(register_1_q), .b({26{1'b1}}), .out({adder_1_out, adder_1_out_2}));  // open: cin, cout
  Multiplexer #(.width(26), .disabled(0), .enable("false")) multiplexer_1 (
    .in0({adder_1_out, adder_1_out_2}), .in1({adder_1_out, rom_1_out_2}), .out(multiplexer_1_out),
    .sel(controlunit_1_jal));
  ROM rom_1 (.in_1(register_1_q), .out_2({rom_1_out_2_2, rom_1_out_2}));
  Multiplexer #(.width(26), .disabled(0), .enable("false")) multiplexer_2 (
    .in0({adder_1_out, adder_1_out_2}), .in1(multiplexer_8_out), .out(multiplexer_2_out),
    .sel(controlunit_1_jal));
  ControlUnit controlunit_1 (
    .Op3(rom_1_out_2_2[25]), .RegDst(controlunit_1_regdst), .Op2(rom_1_out_2_2[24]), .Op1(rom_1_out_2_2[23]),
    .Op0(rom_1_out_2_2[22]), .ALUSrc(controlunit_1_alusrc), .Jump(controlunit_1_jump),
    .MemtoReg(controlunit_1_memtoreg), .RegWrite(controlunit_1_regwrite), .MemRead(controlunit_1_memread),
    .MemWrite(controlunit_1_memwrite), .Branch(controlunit_1_branch), .ALUOp1(controlunit_1_aluop0[1]),
    .ALUOp0(controlunit_1_aluop0[0]), .jr(controlunit_1_jr), .jal(controlunit_1_jal));
  Multiplexer #(.width(4), .disabled(0), .enable("false")) multiplexer_3 (
    .in0(rom_1_out_2_2[17:14]), .in1(rom_1_out_2[13:10]), .out(multiplexer_3_out), .sel(controlunit_1_regdst));
  assign bit_extender_1_out = {{12{1'b0}}, rom_1_out_2};  // Bit_Extender bit_extender_1
  RegisterFile registerfile_1 (
    .Write_ENABLE(controlunit_1_regwrite), .WriteReg(multiplexer_3_out), .in_5(multiplexer_2_out),
    .out_7(registerfile_1_out_7), .ReadReg1(rom_1_out_2_2[21:18]), .out_8(registerfile_1_out_8),
    .ReadReg2(rom_1_out_2_2[17:14]));  // open: Clock
  Adder #(.width(26)) adder_2 (
    .a({adder_1_out, adder_1_out_2}), .b(bit_extender_1_out), .out(adder_2_out));  // open: cin, cout
  Multiplexer #(.width(26), .disabled(0), .enable("false")) multiplexer_4 (
    .in0({adder_1_out, adder_1_out_2}), .in1(adder_2_out), .out(multiplexer_4_out), .sel(and_1_out));
  Multiplexer #(.width(26), .disabled(0), .enable("false")) multiplexer_5 (
    .in0(registerfile_1_out_8), .in1(bit_extender_1_out), .out(multiplexer_5_out), .sel(controlunit_1_alusrc));
  ALUControl alucontrol_1 (
    .ALUOp(controlunit_1_aluop0), .ALUControl(alucontrol_1_alucontrol), .Function(rom_1_out_2[4:0]));
  and and_1 (and_1_out, controlunit_1_branch, alu_1_out_5);
  ALU alu_1 (
    .in_1(registerfile_1_out_7), .in_2(multiplexer_5_out), .ALU_OP(alucontrol_1_alucontrol),
    .out_4(alu_1_out_4), .out_5(alu_1_out_5));
  Multiplexer #(.width(26), .disabled(0), .enable("false")) multiplexer_6 (
    .in0(multiplexer_4_out), .in1(multiplexer_1_out), .out(multiplexer_6_out), .sel(controlunit_1_jump));
  Multiplexer #(.width(26), .disabled(0), .enable("false")) multiplexer_7 (
    .in0(multiplexer_6_out), .in1(registerfile_1_out_7), .out(multiplexer_7_out), .sel(controlunit_1_jr));
  RAM ram_1 (
    .in_1(alu_1_out_4), .in_2(registerfile_1_out_8), .MemWrite(controlunit_1_memwrite),
    .MemRead(controlunit_1_memread), .out_6(ram_1_out_6), .in_5(clock_1_out));
  Multiplexer #(.width(26), .disabled(0), .enable("false")) multiplexer_8 (
    .in0(alu_1_out_4), .in1(ram_1_out_6), .out(multiplexer_8_out), .sel(controlunit_1_memtoreg));

  // Notes on the sheet:
  //   pc
  //   INSTRUCTİON MEMORY
  //   REGİSTER 
  //   ALU
  //   DATA MEMORY
endmodule
